# Fritzing sketch Yukita_Diagram_V0.2.0 (saved by Fritzing 0.9.0b)
breadboards: 1

parts:
  Part1 = Arduino Ethernet Shield (Rev3)
  LED3 = smd LED [color="White (4500K)" package="1206 [SMD]"]
  LED4 = RGB LED (com. cathode, rbg) [package="5 mm [THT]"]

nets:
  N1: Part1.GND, LED3.cathode, LED4.common_cathode
  N2: Part1.PWM_D9, LED3.anode
  N3: Part1.PWM_D3, LED4.green_anode
  N4: Part1.PWM_D5, LED4.blue_anode
  N5: Part1.PWM_D6, LED4.red_anode
